// Logisim project logism_design.circ as structural Verilog: 9 circuits, main circuit processor
module processor (
  input  [17:0] ASSEMBLY_INPUT
);


  // Other names for the same wires on the sheet: ADDR[9:0] = ASSEMBLY_INPUT[13:4]; REG0[3:0] = ASSEMBLY_INPUT[7:4];
  //   REG1[3:0] = ASSEMBLY_INPUT[11:8]; IMM[5:0] = ASSEMBLY_INPUT[17:12]; REG2[3:0] = ASSEMBLY_INPUT[15:12]

  // Notes on the sheet:
  //   OP CODE
endmodule

module half_adder (
  input  A,
  input  B,
  output out_3,
  output out_4
);

  xor xor_1 (out_3, A, B);
  and and_1 (out_4, A, B);
endmodule

module full_adder (
  input  in_1,
  input  in_2,
  input  in_3,
  output out_4,
  output out_5
);

  wire and_1_out, and_2_out, xor_1_out;

  xor xor_1 (xor_1_out, in_1, in_2);
  xor xor_2 (out_4, xor_1_out, in_3);
  and and_1 (and_1_out, xor_1_out, in_3);
  and and_2 (and_2_out, in_2, in_1);
  or or_1 (out_5, and_1_out, and_2_out);
endmodule

module _2_bit_adder (
  input  [1:0] A,
  input  [1:0] B,
  input  C,
  output [1:0] sum,
  output out_5
);

  wire full_adder_1_out_5;

  full_adder full_adder_1 (.in_1(A[0]), .in_2(B[0]), .in_3(C), .out_4(sum[0]), .out_5(full_adder_1_out_5));
  full_adder full_adder_2 (.in_1(A[1]), .in_2(B[1]), .in_3(full_adder_1_out_5), .out_4(sum[1]), .out_5(out_5));
endmodule

module _4_bit_adder (
  input  [3:0] A,
  input  [3:0] B,
  input  C,
  output out_4,
  output [3:0] out_5
);

  wire n2_bit_adder_1_p5;

  // _2_bit_adder 2_bit_adder_1: pin names not known; wires that end beside it: A[1:0], B[1:0], C, out_5[1:0], n2_bit_adder_1_p5
  // _2_bit_adder 2_bit_adder_2: pin names not known; wires that end beside it: A[3:2], B[3:2], n2_bit_adder_1_p5, out_5[3:2], out_4
endmodule

module _8_bit_adder (
  input  [7:0] in_1,
  input  [7:0] in_2,
  input  in_3,
  output out_4,
  output [7:0] out_5
);

  wire n4_bit_adder_1_out_4;

  _4_bit_adder u_4_bit_adder_1 (
    .A(in_1[3:0]), .B(in_2[3:0]), .C(in_3), .out_4(n4_bit_adder_1_out_4), .out_5(out_5[3:0]));
  _4_bit_adder u_4_bit_adder_2 (
    .A(in_1[7:4]), .B(in_2[7:4]), .C(n4_bit_adder_1_out_4), .out_4(out_4), .out_5(out_5[7:4]));
endmodule

module _16_bit_adder (
  input  [15:0] in_1,
  input  [15:0] in_2,
  input  in_3,
  output out_4,
  output [15:0] out_5
);

  wire n8_bit_adder_1_out_4;

  _8_bit_adder u_8_bit_adder_1 (
    .in_1(in_1[7:0]), .in_2(in_2[7:0]), .in_3(in_3), .out_4(n8_bit_adder_1_out_4), .out_5(out_5[7:0]));
  _8_bit_adder u_8_bit_adder_2 (
    .in_1(in_1[15:8]), .in_2(in_2[15:8]), .in_3(n8_bit_adder_1_out_4), .out_4(out_4), .out_5(out_5[15:8]));
endmodule

module ALU (
);


  // Notes on the sheet:
  //   ADD
  //   AND
  //   NAND
  //   XOR
endmodule

module _18_bit_adder (
  input  [17:0] A,
  input  [17:0] B,
  input  C
);

  wire full_adder_5_out_4, full_adder_5_out_5, full_adder_6_out_4, full_adder_6_out_5, full_adder_7_out_4,
       full_adder_7_out_5, full_adder_8_out_5, full_adder_9_out_5;

  full_adder full_adder_1 ();  // open: in_1, in_2, in_3, out_4, out_5
  full_adder full_adder_2 ();  // open: in_1, in_2, in_3, out_4, out_5
  full_adder full_adder_3 ();  // open: in_1, in_2, in_3, out_4, out_5
  full_adder full_adder_4 ();  // open: in_1, in_2, in_3, out_4, out_5
  full_adder full_adder_5 (.in_1(C), .in_2(A[0]), .in_3(B[0]), .out_4(full_adder_5_out_4), .out_5(full_adder_5_out_5));
  full_adder full_adder_6 (
    .in_1(full_adder_5_out_5), .in_2(A[1]), .in_3(B[1]), .out_4(full_adder_6_out_4),
    .out_5(full_adder_6_out_5));
  full_adder full_adder_7 (
    .in_1(full_adder_6_out_5), .in_2(A[2]), .in_3(B[2]), .out_4(full_adder_7_out_4),
    .out_5(full_adder_7_out_5));
  full_adder full_adder_8 (
    .in_1(full_adder_7_out_5), .in_2(A[3]), .in_3(B[3]), .out_5(full_adder_8_out_5));  // open: out_4
  full_adder full_adder_9 (
    .in_1(full_adder_8_out_5), .in_2(A[4]), .in_3(B[4]), .out_5(full_adder_9_out_5));  // open: out_4
  full_adder full_adder_10 (.in_1(full_adder_9_out_5));  // open: in_2, in_3, out_4, out_5
  full_adder full_adder_11 ();  // open: in_1, in_2, in_3, out_4, out_5
  full_adder full_adder_12 ();  // open: in_1, in_2, in_3, out_4, out_5
  full_adder full_adder_13 ();  // open: in_1, in_2, in_3, out_4, out_5
  full_adder full_adder_14 ();  // open: in_1, in_2, in_3, out_4, out_5
  full_adder full_adder_15 ();  // open: in_1, in_2, in_3, out_4, out_5
  full_adder full_adder_16 ();  // open: in_1, in_2, in_3, out_4, out_5
endmodule
